# Fritzing sketch WiringDiagram (saved by Fritzing 0.9.3b)

parts:
  Part1 = Arduino Mega 2560 (Rev3)
  VCC1 = 4 x AAA Battery Mount  # not connected
  MOTOR1 = Adafruit Gear-Reduced Stepper Motor (small)
  Part2 = EasyDriver_v44

nets:
  GND: Part1.GND, Part2.GND
  5V: Part1.5V, Part2.VCC
  N1: MOTOR1.RED, Part2.OUT2A
  N2: MOTOR1.ORANGE, Part2.OUT2B
  N3: MOTOR1.YELLOW, Part2.OUT1A
  N4: MOTOR1.PINK, Part2.OUT1B
  N5: MOTOR1.BLUE, Part2.PFD

notes:
  Use the 9V battery to barrel connector here
  They didn't have the stepper motor controller image, so you'll have to pretend a bit
  On the real board you'll just plug the motor connector in to the board, very simple
  You'll connect pins IN1, IN2, IN3, IN4 from the controller board to the arduino. You can choose any of the 0-13 pins but you'll need to update the code to use the same pins

custom parts:
  Adafruit Gear-Reduced Stepper Motor (small): Adafruit gear-reduction stepper motor (small)
